# Fritzing sketch Web2RGB-LED (saved by Fritzing 0.9.0b)
breadboards: 1

parts:
  Bauteil1 = Arduino Uno (Rev3)
  1_in_3_out = RGB LED (com. cathode, rbg) [package="5 mm [THT]"]
  part = Resistor [tolerance=±5% resistance=150 package=THT]
  part_2 = Resistor [tolerance=±5% resistance=27 package=THT]
  part_3 = Resistor [tolerance=±5% resistance=39 package=THT]

nets:
  N1: Bauteil1.D9_PWM, part.Pin_0
  N2: Bauteil1.D10_PWM/SS, part_2.Pin_0
  N3: Bauteil1.D11_PWM/MOSI, part_3.Pin_0
  N4: Bauteil1.5V, 1_in_3_out.green_anode
  N5: 1_in_3_out.red_anode, part_3.Pin_1
  N6: 1_in_3_out.common_cathode, part_2.Pin_1
  N7: 1_in_3_out.blue_anode, part.Pin_1
